# Fritzing sketch Firefly (saved by Fritzing 0.9.3b)
breadboards: 1

parts:
  S1 = Pushbutton [package="[THT]"]
  Part1 = Arduino Nano (Rev3.0)
  Part2 = NRF24L01+ Breakout Board
  OLED_I2C1 = OLED 128x64 I2C Monochrome Display
  R2 = Resistor [tolerance=±5% resistance=220 package=THT]
  BAT1 = Battery Holders [package=battcom_20mm_pth]
  BAT2 = Battery Holders [package=battcom_20mm_pth]
  S2 = Toggle Switch [package=THT]

nets:
  N1: S1.Pin_1, S1.Pin_2, Part1.D2, R2.Pin_1
  5V: S1.Pin_3, S1.Pin_4, Part1.5V, OLED_I2C1.VDD
  GND: Part1.GND, Part2.GND, OLED_I2C1.GND, R2.Pin_0, S2.COM
  N2: Part1.D10, Part2.CS
  N3: Part1.D11/MOSI, Part2.MOSI
  N4: Part1.D12/MISO, Part2.MISO
  N5: Part1.VIN, BAT1.+
  N6: Part1.A5, OLED_I2C1.SCK
  N7: Part1.A4, OLED_I2C1.SDA
  3V3: Part1.3V3, Part2.VCC
  N8: Part1.D13/SCK, Part2.SCK
  N9: BAT1.-, BAT2.+
  N10: BAT2.-, S2.L2

notes:
  Double-check your OLED pins match below (and adjust as needed) as they can vary across manufacturers.
  Please make sure the nRF24L01 module is connected to 3.3v only. Any higher may damage it.
  We use two CR2032 (3v each) cells in series for 6v. Any 6v - 20v power supply may be substituted.
